// Logisim project max1s.circ as structural Verilog: 3 circuits, main circuit max1s
module max1s (
  input  [31:0] x,
  input  clk,
  input  start,
  output rdy,
  output [5:0] max1s
);

  wire or_1_out;
  wire [5:0] adder_1_out, multiplexer_2_out;
  wire [31:0] _32_out, multiplexer_1_out, shifter_1_out, XReg_q;

  Multiplexer #(.width(32), .disabled(0), .enable("false")) multiplexer_1 (
    .in0(_32_out), .in1(x), .out(multiplexer_1_out), .sel(start));
  Register #(.width(32), .trigger("falling")) XReg (.D(multiplexer_1_out), .Q(XReg_q), .clk(clk));  // open: en, clr
  Adder #(.width(6)) adder_1 (.a(6'b000001), .b(max1s), .out(adder_1_out));  // open: cin, cout
  assign _32_out = XReg_q & shifter_1_out;  // AND_Gate _32, 32 bits wide
  Shifter #(.width(32)) shifter_1 (.in(XReg_q), .\dist (5'b00001), .out(shifter_1_out));
  Multiplexer #(.width(6), .disabled(0), .enable("false")) multiplexer_2 (
    .in0(adder_1_out), .in1({6{1'b0}}), .out(multiplexer_2_out), .sel(start));
  or or_1 (or_1_out, start, ~rdy);  // OR_Gate
  Register #(.width(6), .trigger("falling")) Max1sReg (
    .D(multiplexer_2_out), .en(or_1_out), .Q(max1s), .clk(clk));  // open: clr
  Comparator #(.width(32)) comparator_1 (.a(XReg_q), .b({32{1'b0}}), .eq(rdy));  // open: gt, lt

  // Notes on the sheet:
  //   if (start || !rdy)
  //   rdy de 1 bit está calculado como: XReg == 0
  //   XReg = start ? x : (XReg & (XReg<<1)
  //   Max1sReg = Max1sReg + 1
  //   La entrada de XReg es:
  //   Si start es 1 : la entrada x
  //   sino : XReg & ( XReg << 1)
  //   Los registros XReg y Max1sReg se calculan en el pulso de bajada del reloj como:
  //   Circuito que calcula la máxima cantidad de unos consecutivos en la entrada x
  //   La entrada de Max1sReg es:
  //   Si start es 1 : 0
  //   sino si rdy es 1 : XReg
  //   sino : XReg+1
  //   Algoritmo:
  //     int max1s= 0;
  //     while (x!=0) {
  //       x = x & (x>>1);
  //       max1s++;:
  //     }
  //     return max1s;
  //     }
  //   unsigned int calc(unsigned int x) {:
endmodule

module test (
  output [5:0] out_1
);

  wire Clk_out, max1s_1_rdy, tester_1_clk_out, tester_1_fail, tester_1_start, tester_1_success;
  wire [31:0] tester_1_x;

  // Probe on tester_1_x
  Clock Clk (.out(Clk_out));
  LED led_1 (.in(tester_1_fail));
  max1s max1s_1 (.x(tester_1_x), .start(tester_1_start), .clk(tester_1_clk_out), .max1s(out_1), .rdy(max1s_1_rdy));
  tester tester_1 (
    .clk_in(Clk_out), .max1s(out_1), .rdy(max1s_1_rdy), .x(tester_1_x), .start(tester_1_start),
    .clk_out(tester_1_clk_out), .fail(tester_1_fail), .success(tester_1_success));
  LED led_2 (.in(tester_1_success));
  // Probe on out_1
  // Probe on max1s_1_rdy

  // Notes on the sheet:
  //   Red means failure:
  //   The output max1s
  //   is not the max number
  //   of consecutive 1s
  //   Green means success
  //   Your solution matches
  //   the full timing diagram
  //   Congratulations!
  //   The bug in T2 was corrected
  //   Run the whole test with control-R control-K
  //   You don´t need to step manually the clock with control-T
endmodule

module tester (
  input  rdy,
  input  [5:0] max1s,
  input  clk_in,
  output [31:0] x,
  output start,
  output success,
  output fail,
  output clk_out
);

  wire and_1_out, comparator_1_eq, d_ff_1_q;
  wire [4:0] counter_1_q;
  wire [23:0] rom_1_data;

  Pull_Resistor pull_resistor_1 (.node(rdy));
  Pull_Resistor pull_resistor_2 (.node(max1s));
  D_Flip_Flop #(.trigger("falling")) d_ff_1 (.clk(clk_in), .D(1'b1), .Q(d_ff_1_q));  // open: Qn, preset, en, reset
  and and_1 (and_1_out, d_ff_1_q, rdy, ~fail, ~rom_1_data[12]);  // AND_Gate
  Counter #(.width(5), .max('h1f), .trigger("falling")) counter_1 (
    .count(and_1_out), .Q(counter_1_q), .clk(clk_in));  // open: load, D, carry, clr
  ROM #(.addrWidth(5), .dataWidth(24)) rom_1 (
    .addr(counter_1_q), .data({rom_1_data[23:9], start, rom_1_data[7:0]}));  // open: sel
  Comparator #(.width(6)) comparator_1 (.a(rom_1_data[21:16]), .b(max1s), .eq(comparator_1_eq));  // open: gt, lt
  ROM #(.addrWidth(3), .dataWidth(32)) rom_2 (.addr(rom_1_data[2:0]), .data(x));  // open: sel
  and and_2 (success, rom_1_data[12], rdy, comparator_1_eq);
  and and_3 (fail, rom_1_data[4], rdy, ~comparator_1_eq);  // AND_Gate
  and and_4 (clk_out, ~fail, clk_in);  // AND_Gate

  // Notes on the sheet:
  //   max1[21:16] success[12] start[8]  valid[4] ex[1-0] 
  //   contents of rom_1 (hex, n*v repeats v):
  //   0 100 10010 10010 101 30011 102 70012 70012 103 180013 180013 180013 104 10 10 105 4*200015 201015
  //   contents of rom_2 (hex, n*v repeats v):
  //   100 380030 307f07 ffffff0 0 ffffffff
endmodule
