// Logisim project test.circ as structural Verilog: 1 circuit, main circuit main
module main (
  input  in_1,
  input  [7:0] in_2,
  input  in_3,
  output out_4,
  output out_5
);

  wire and_1_out, comparator_1_eq, or_1_out;
  wire [7:0] adder_1_out, multiplexer_1_out, register_1_q, rom_1_data;

  // Probe on in_2
  Adder adder_1 (.a(register_1_q), .b(8'h1), .out(adder_1_out));  // open: cin, cout
  Multiplexer #(.width(8)) multiplexer_1 (
    .in0(adder_1_out), .in1({8{1'b0}}), .out(multiplexer_1_out), .sel(in_1));  // open: en
  // Probe on or_1_out
  or or_1 (or_1_out, in_1, and_1_out);
  Register #(.trigger("falling")) register_1 (
    .D(multiplexer_1_out), .en(or_1_out), .Q(register_1_q), .clk(in_3));  // open: clr
  // Probe on register_1_q
  Comparator comparator_1 (.a(register_1_q), .b(8'hf), .eq(comparator_1_eq));  // open: gt, lt
  and and_1 (and_1_out, ~comparator_1_eq, ~out_5);  // AND_Gate
  ROM rom_1 (.addr(register_1_q), .data(rom_1_data));  // open: sel
  Comparator comparator_2 (.a(in_2), .b(rom_1_data), .eq(out_5));  // open: gt, lt
  or or_2 (out_4, comparator_1_eq, out_5);

  // Notes on the sheet:
  //   contents of rom_1 (hex, n*v repeats v):
  //   a5 2b 4f 82 d 11 13 17 1d 1f 25 29 2b 2f 35 3b 239*0 3b
endmodule
